# Fritzing sketch Schematic (saved by Fritzing 0.9.3b)
circuit board: 8.46667cm x 5.64444cm
breadboards: 1

parts:
  Node_Mcu = NodeMCU V1.0
  HC-SR04_Sensor_1 = HC-SR04 Ultrasonic Distance Sensor
  Buzzer = Piezo Speaker
  5v_battery_supply = Battery Holders [package=battcon_12mm_pth]

nets:
  N1: Node_Mcu.D1, HC-SR04_Sensor_1.TRIG
  N2: Node_Mcu.D3, HC-SR04_Sensor_1.ECHO
  GND: Node_Mcu.GND, HC-SR04_Sensor_1.GND, Buzzer.pin1, 5v_battery_supply.-
  N3: Node_Mcu.D7, Buzzer.pin2
  VIN: Node_Mcu.Vin, HC-SR04_Sensor_1.VCC, 5v_battery_supply.+

custom parts:
  NodeMCU V1.0: ESP8266 based NodeMCU
