# Fritzing sketch Locking unlocking of door using arduino (saved by Fritzing 0.9.3b)
breadboards: 1

parts:
  Part1 = Arduino Uno (Rev3) - ICSP
  Part2 = Bluetooth HC-05 Macho
  IC1 = L293D [package=THT]
  M1 = DC Motor
  VCC1 = Battery block 9V

nets:
  5V: Part1.5V, Part2.VCC, IC1.Enable_1, IC1.+V
  GND: Part1.GND, Part2.GND, IC1.0V, VCC1.-, VCC1.+
  N1: Part1.D9_PWM, IC1.In_1, IC1.In_4
  N2: Part1.D10_PWM/SS, IC1.In_2, IC1.In_3
  N3: Part1.D0/RX, Part2.RXD
  N4: Part1.D1/TX, Part2.TXD
  N5: IC1.Out_1_(_Controlled_by_Enable_1_), IC1.Out_4_(_Controlled_by_Enable_2_), M1.pin_1
  N6: IC1.Out_2_(_Controlled_by_Enable_1_), IC1.Out_3_(_Controlled_by_Enable_2_), M1.pin_2
  N7: IC1.+Vmotor, IC1.Enable_2
