# Fritzing sketch Alcohol Detection (saved by Fritzing 0.9.3b)
breadboards: 1

parts:
  Part1 = Arduino Uno (Rev3)
  U1 = GAS_SENSOR [package=mq-3]
  LCD1 = LCD screen
  J1 = Piezo Speaker
  R1 = Resistor [tolerance=±5% resistance=220 package=THT]  # not connected
  U2 = SWITCH-SPST-2 [package=switch-spst-vertical]
  VCC1 = Battery block 9V

nets:
  N1: Part1.A0, U1.B1
  N2: Part1.D8, LCD1.DB4
  N3: Part1.D9_PWM, LCD1.DB7
  N4: Part1.D12/MISO, LCD1.DB6
  N5: Part1.D2, J1.pin2
  N6: Part1.D4, LCD1.DB0
  N7: Part1.D5_PWM, LCD1.DB1
  N8: Part1.D6_PWM, LCD1.DB2
  N9: Part1.D7, LCD1.DB3
  5V: Part1.5V, LCD1.VDD, LCD1.LED+
  GND: Part1.GND, LCD1.VSS, LCD1.DB5, LCD1.LED-, VCC1.-
  N10: Part1.VIN, U2.O
  N11: U1.A1, U1.H1
  N12: U1.H2, J1.pin1
  N13: U2.P, VCC1.+
