# Fritzing sketch garage door (saved by Fritzing 0.9.3b)
breadboards: 1

parts:
  Part1 = Arduino Uno (Rev3) - ICSP
  Part2 = EasyDriver_v44
  Part3 = Bluetooth HC-05 Macho
  M1 = Stepper Motor - Bipolar
  Part4 = Lilypad Battery Connect

nets:
  5V: Part1.5V, Part3.VCC
  N1: Part1.D8, Part2.DIR
  N2: Part1.D9_PWM, Part2.STEP
  N3: Part1.D0/RX, Part3.TXD
  N4: Part1.D1/TX, Part3.RXD
  N5: Part1.VIN, Part4.+
  GND: Part2.GND, Part3.GND, Part4.-
  N6: Part2.OUT2A, M1.A
  N7: Part2.OUT2B, M1.C
  N8: Part2.OUT1A, M1.B
  N9: Part2.OUT1B, M1.D
