# Fritzing sketch Simple weather station (saved by Fritzing 0.9.3b)
circuit board: 8.46667cm x 5.64444cm
breadboards: 1

parts:
  U1 = NodeMCU V1.0
  DHT1 = DHT11 Humitidy and Temperature Sensor
  Part1 = Adafruit BMP180
  R1 = 220 Ω Resistor [package="0402 [SMD]"]
  R2 = 220 Ω Resistor [package="0402 [SMD]"]
  R4 = Photocell (LDR) [package=THT]
  VCC1 = Battery block 9V

nets (from the breadboard view):
  N1: U1.D1, Part1.SCL
  N2: U1.D2, Part1.SDA
  N3: U1.D4, DHT1.DATA, R1.Pin_1
  3V3: U1.3V3, DHT1.VDD, Part1.+3V3, R1.Pin_0
  GND: U1.GND, DHT1.GND, Part1.GND, VCC1.-
  N4: U1.Vin, VCC1.+
  N5: U1.A0, R4.pin_1
  N6: R2.Pin_1, R4.pin_0

custom parts:
  NodeMCU V1.0: ESP8266 based NodeMCU
  DHT11 Humitidy and Temperature Sensor: DHT11 Humidity and Temperature Sensor
  Adafruit BMP180: This precision sensor from Bosch is the best low-cost sensing solution for measuring barometric pressure and temperature. Because pressure changes with altitude you can also use it as an altimeter! The sensor is soldered onto a PCB with a 3.3V regulator, I2C level shifter and pull-up resistors on the I2C pins. The BMP180 is the next-generation of sensors from Bosch, and replaces the BMP085.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
  220 Ω Resistor: Resistor Basic schematic elements and footprints for 0603, 1206, and PTH resistors.
